# Fritzing sketch tiny_watchdog (saved by Fritzing 0.9.1b)
circuit board: 8.46667cm x 5.64444cm
breadboards: 1

parts:
  Part1 = Arduino Uno (Rev3)
  U1 = attiny85 [package=dip]
  U2 = POT [package=alps_pot]
  JP1 = Header 1 [package=1x01_offset]
  JP2 = Header 1 [package=1x01_offset]
  LED1 = smd LED [color="Red (635nm)" package="0805 [SMD]"]
  R1 = Resistor [tolerance=±5% resistance=220 package=THT]
  D1 = Rectifier Diode [part_number=1N4001 package="300 mil [THT]"]

nets (from the breadboard view):
  N1: Part1.A2, U1.Pin_6
  N2: Part1.RESET, D1.anode
  N3: Part1.5V, U1.Pin_8, U2.A
  N4: Part1.GND, U1.Pin_4, U2.E, JP2.1, R1.Pin_0
  N5: U1.Pin_2, U2.S
  N6: U1.Pin_3, JP1.1
  N7: U1.Pin_5, LED1.anode
  N8: U1.Pin_7, D1.cathode
  N9: LED1.cathode, R1.Pin_1

notes:
  3: input pot
  2: output reset
  1: input pat
  4: input time multiplier (jumper)
  0: output LED
