# Fritzing sketch uno_watchdog (saved by Fritzing 0.9.1b)
breadboards: 1

parts:
  Part1 = Arduino Uno (Rev3)
  R1 = Rotary Potentiometer (Small) [maximum_resistance=100kΩ package=THT]
  Part2 = Arduino Uno (Rev3)
  JP1 = Header 1 [package=1x01_offset]
  JP2 = Header 1 [package=1x01_offset]
  D1 = Rectifier Diode [part_number=1N4001 package="300 mil [THT]"]

nets:
  N1: Part1.A2, R1.wiper
  N2: Part1.D10_PWM/SS, JP1.1
  N3: Part1.D13/SCK, D1.cathode
  N4: Part1.D4, Part2.A2
  5V: Part1.5V, R1.leg1, Part2.5V
  GND: Part1.GND, R1.leg2, Part2.GND, JP2.1
  N5: Part2.RESET, D1.anode

notes:
  A2 - input: read pot
  13 - output: reset arduino 2
  10 - input: read jumper multiplier setting (LOW = ON)
  4 - input: receive dog pat
  - after calibration, draw dual ring time scale around pot -
  Watchdog
